# Fritzing sketch Serra (saved by Fritzing 0.9.10b)
circuit board: 8.46667cm x 5.64444cm
breadboards: 1

parts:
  Display = Grove OLED 128x96
  Soil = Soil Moisture Sensor
  Part2 = Arduino Uno (Rev3)
  R2 = Resistor [tolerance=±5% resistance=10k package="0603 [SMD]"]
  R1 = PHOTOCELL [package=photocell-kit]
  LED_strip = WS2812 RGB LED matrix 1x8  # not connected
  S1 = Taiway 100-SP-X-T1 SPDT Miniature Toggle Switch [part_number=100-SP-X-T1-0-0-B1-M1 package=THT]  # not connected
  Water_Pump = water pump/motor  # not connected
  Fan1 = DC Motor [voltage_(max)=6V voltage_(min)=3V]  # not connected
  Fan2 = DC Motor [voltage_(max)=6V voltage_(min)=3V]  # not connected
  RHT2 = Humidity and Temperature Sensor RHT03  # not connected

nets:
  GND: Display.GND, Soil.GND, Part2.GND, R2.Pin_0
  VCC: Display.VCC, Soil.VCC, Part2.5V, R1.P$1
  N1: Display.SDA, Part2.A4/SDA
  N2: Display.SCL, Part2.A5/SCL
  N3: Part2.A0, R2.Pin_1, R1.P$2

notes:
  switch
  ventole
  Sensori
  Attuatori

custom parts:
  WS2812 RGB LED matrix 1x8: WS2812 matrix 1x8
  water pump/motor: WATER PUMP BY ARDUBLOCKTR
